// Logisim project hw4.circ as structural Verilog: 18 circuits, main circuit main
module main (
  input  reset
);

  wire ALU_blt, ALU_bne, ALUImm, ALUOp, blt, blt_out, bne, bne_out, Clk, jal, jr, jump, keyboard,
       keyboard_1_avail, lw_sw, not_1_out, not_2_out, not_3_out, not_5_out, Rdst, sw, TTYWE, WE;
  wire [2:0] alu_control_1_alu_optype, controlled_buffer_1_out, multiplexer_3_out, rd, rs, rt, shamt;
  wire [3:0] mips_instr_div_1_opcode;
  wire [5:0] imm;
  wire [6:0] keyboard_1_data;
  wire [7:0] rt_val;
  wire [11:0] address;
  wire [15:0] alu_1_1_out_5, alu_adder_pc_bne_1_address, alu_adder_pc_bne_2_address, alu_pc_j_1_jump_address,
       multiplexer_1_out, multiplexer_2_out, multiplexer_4_out, multiplexer_5_out, multiplexer_6_out,
       multiplexer_7_out, multiplexer_8_out, multiplexer_9_out, PC_1, pc_1_address_out, ram_1_data,
       registerfile_1_readdata2, rom_1_data, rs_val, SignEx;

  Clock clock_1 (.out(Clk));
  PC u_pc_1 (.Address_in(multiplexer_9_out), .Clock(Clk), .reset(reset), .Address_out(pc_1_address_out));
  ALU_PC alu_pc_1 (.Input(pc_1_address_out), .out_2(PC_1));
  ROM #(.addrWidth(16), .dataWidth(16)) rom_1 (.addr(pc_1_address_out), .data(rom_1_data));  // open: sel
  MIPS_Instr_Div mips_instr_div_1 (
    .MIPS(rom_1_data), .Shamt(shamt), .Rd(rd), .Rt(rt), .Rs(rs), .Opcode(mips_instr_div_1_opcode),
    .Immediate(imm), .Address(address));
  ALU_Adder___PC_bne alu_adder_pc_bne_1 (.PC(PC_1), .imm(SignEx), .Address(alu_adder_pc_bne_1_address));
  Multiplexer #(.width(16), .enable("false")) multiplexer_1 (
    .in0(PC_1), .in1(alu_adder_pc_bne_1_address), .out(multiplexer_1_out), .sel(bne_out));
  and u_bne (bne_out, bne, ALU_bne);
  Multiplexer #(.width(16), .enable("false")) multiplexer_2 (
    .in0(multiplexer_8_out), .in1({{8{1'b0}}, rt_val}), .out(multiplexer_2_out), .sel(keyboard));
  assign controlled_buffer_1_out = not_1_out ? rd : 3'bz;  // Controlled_Buffer controlled_buffer_1
  not not_1 (not_1_out, jal);
  assign controlled_buffer_1_out = jal ? 3'b111 : 3'bz;  // Controlled_Buffer controlled_buffer_2
  Control control_1 (
    .Instr_Optype(mips_instr_div_1_opcode), .keyboard(keyboard), .jal(jal), .jump(jump), .blt(blt),
    .bne(bne), .lw_sw(lw_sw), .sw(sw), .ALUimm(ALUImm), .WE(WE), .Rdst(Rdst), .ALUOp(ALUOp), .jr(jr),
    .TTYWE(TTYWE));
  Multiplexer #(.width(3), .enable("false")) multiplexer_3 (
    .in0(rt), .in1(controlled_buffer_1_out), .out(multiplexer_3_out), .sel(Rdst));
  not not_2 (not_2_out, Clk);
  RegisterFile registerfile_1 (
    .Reset(reset), .ReadReg1(rs), .ReadReg2(rt), .Input(multiplexer_2_out), .RegWriteEnable(WE),
    .Clock(not_2_out), .WriteReg(multiplexer_3_out), .ReadData1(rs_val), .ReadData2(registerfile_1_readdata2));
  ALU_Adder___PC_bne alu_adder_pc_bne_2 (.PC(PC_1), .imm(SignEx), .Address(alu_adder_pc_bne_2_address));
  and u_blt (blt_out, blt, ALU_blt);
  Sign_Extention sign_extention_1 (.Imm(imm), .\output (SignEx));
  TTY #(.rows(13), .cols(80), .trigger("falling")) tty_1 (.data(rs_val[6:0]), .clk(Clk), .we(TTYWE), .clr(reset));
  Multiplexer #(.width(16), .enable("false")) multiplexer_4 (
    .in0(multiplexer_1_out), .in1(alu_adder_pc_bne_2_address), .out(multiplexer_4_out), .sel(blt_out));
  Multiplexer #(.width(16), .enable("false")) multiplexer_5 (
    .in0(registerfile_1_readdata2), .in1(SignEx), .out(multiplexer_5_out), .sel(ALUImm));
  ALU_Control alu_control_1 (
    .ALU_Instruction(mips_instr_div_1_opcode), .ALU_optype(alu_control_1_alu_optype), .Control(ALUOp));
  ALU__1 alu_1_1 (
    .OpType(alu_control_1_alu_optype), .input1(rs_val), .input2(multiplexer_5_out), .shamt(shamt),
    .out_5(alu_1_1_out_5), .Z(ALU_bne), .Y(ALU_blt));
  ALU_PC_J alu_pc_j_1 (.Jump(address), .PC(PC_1), .Jump_Address(alu_pc_j_1_jump_address));
  Multiplexer #(.width(16), .enable("false")) multiplexer_6 (
    .in0(multiplexer_4_out), .in1(alu_pc_j_1_jump_address), .out(multiplexer_6_out), .sel(jump));
  not not_3 (not_3_out, Clk);
  RAM #(.addrWidth(16), .dataWidth(16), .bus("separate")) ram_1 (
    .addr(alu_1_1_out_5), .din(registerfile_1_readdata2), .data(ram_1_data), .str(sw), .clk(not_3_out));  // open: sel, ld, clr
  Multiplexer #(.width(16), .enable("false")) multiplexer_7 (
    .in0(alu_1_1_out_5), .in1(ram_1_data), .out(multiplexer_7_out), .sel(lw_sw));
  Multiplexer #(.width(16), .enable("false")) multiplexer_8 (
    .in0(multiplexer_7_out), .in1(PC_1), .out(multiplexer_8_out), .sel(jal));
  Keyboard keyboard_1 (.clk(Clk), .re(keyboard), .clr(reset), .avail(keyboard_1_avail), .data(keyboard_1_data));
  Multiplexer #(.width(16), .enable("false")) multiplexer_9 (
    .in0(multiplexer_6_out), .in1(rs_val), .out(multiplexer_9_out), .sel(jr));
  assign rt_val[6:0] = keyboard_1_avail ? keyboard_1_data : 7'bz;  // Controlled_Buffer controlled_buffer_3
  not not_4 (rt_val[7], keyboard_1_avail);
  not not_5 (not_5_out, keyboard_1_avail);
  assign rt_val[6:0] = not_5_out ? {7{1'b0}} : 7'bz;  // Controlled_Buffer controlled_buffer_4

  // Notes on the sheet:
  //   jump/jal
endmodule

module ALU__1 (
  input  [2:0] OpType,
  input  [15:0] input1,
  input  [15:0] input2,
  input  [2:0] shamt,
  output [15:0] out_5,
  output Z,
  output Y
);

  wire n16_adder_2_ovf, out6;
  wire [15:0] out0, out1, out2, out3, out4, out5;

  _16_Adder u_16_adder_1 (.sub(1'b0), .result(out0), .A(input1), .B(input2));  // open: ovf
  _16_Adder u_16_adder_2 (.ovf(n16_adder_2_ovf), .sub(1'b1), .result(out1), .A(input1), .B(input2));
  assign out2 = ~input1;  // NOT_Gate not_1, 16 bits wide
  assign out3 = input1 ^ input2;  // XOR_Gate xor_1, 16 bits wide
  Left_Shifter left_shifter_1 (.Input(input1), .Output(out4), .in_2(shamt));
  Right_Shifter right_shifter_1 (.Input(input1), .Output(out5), .in_2(shamt));
  Equality_Comparator equality_comparator_1 (.A(input1), .B(input2), .out_3(out6));
  xor xor_2 (Y, out1[15], n16_adder_2_ovf);
  Multiplexer #(.select(3), .width(16), .enable("false")) multiplexer_1 (
    .in0(out0), .in1(out1), .in2(out2), .in3(out3), .in4(out4), .in5(out5), .out(out_5), .sel(OpType));  // open: in6, in7
  not not_2 (Z, out6);

  // Other names for the same wires on the sheet: in1[15:0] = input1; in2[15:0] = input2; OT[2:0] = OpType

  // Notes on the sheet:
  //   Not equal = 1
  //   equal = 0
  //   A<B = 1
endmodule

module Sign_Extention (
  input  [5:0] Imm,
  output [15:0] \output 
);


  assign \output  = {{11{Imm[5]}}, Imm[4:0]};
endmodule

module ALU_PC (
  input  [15:0] Input,
  output [15:0] out_2
);

  _16_Adder u_16_adder_1 (.sub(1'b0), .result(out_2), .A(Input), .B(16'h1));  // open: ovf
endmodule

module _1_bit_adder (
  input  A,
  input  B,
  input  Cin,
  output Sum,
  output Cout
);

  wire and_1_out, and_2_out, and_3_out, xor_1_out;

  xor xor_1 (xor_1_out, A, B);
  and and_1 (and_1_out, A, B);
  and and_2 (and_2_out, A, Cin);
  and and_3 (and_3_out, B, Cin);
  xor xor_2 (Sum, xor_1_out, Cin);
  or or_1 (Cout, and_1_out, and_2_out, and_3_out);
endmodule

module _16_Adder (
  input  [15:0] B,
  input  [15:0] A,
  input  sub,
  output ovf,
  output [15:0] result
);

  wire n1_bit_adder_1_cout, n1_bit_adder_2_cout, n1_bit_adder_3_cout, n1_bit_adder_4_cout,
       n1_bit_adder_5_cout, n1_bit_adder_6_cout, n1_bit_adder_7_cout, n1_bit_adder_8_cout,
       n1_bit_adder_9_cout, n1_bit_adder_10_cout, n1_bit_adder_11_cout, n1_bit_adder_12_cout,
       n1_bit_adder_13_cout, n1_bit_adder_14_cout, n1_bit_adder_15_cout, n1_bit_adder_16_cout, xor_2_out,
       xor_3_out, xor_4_out, xor_5_out, xor_6_out, xor_7_out, xor_8_out, xor_9_out, xor_10_out, xor_11_out,
       xor_12_out, xor_13_out, xor_14_out, xor_15_out, xor_16_out, xor_17_out;

  xor xor_1 (ovf, n1_bit_adder_1_cout, n1_bit_adder_2_cout);
  xor xor_2 (xor_2_out, sub, B[15]);
  _1_bit_adder u_1_bit_adder_1 (
    .A(A[15]), .B(xor_2_out), .Cin(n1_bit_adder_2_cout), .Sum(result[15]), .Cout(n1_bit_adder_1_cout));
  xor xor_3 (xor_3_out, sub, B[14]);
  _1_bit_adder u_1_bit_adder_2 (
    .A(A[14]), .B(xor_3_out), .Cin(n1_bit_adder_3_cout), .Sum(result[14]), .Cout(n1_bit_adder_2_cout));
  xor xor_4 (xor_4_out, sub, B[13]);
  _1_bit_adder u_1_bit_adder_3 (
    .A(A[13]), .B(xor_4_out), .Cin(n1_bit_adder_4_cout), .Sum(result[13]), .Cout(n1_bit_adder_3_cout));
  xor xor_5 (xor_5_out, sub, B[12]);
  _1_bit_adder u_1_bit_adder_4 (
    .A(A[12]), .B(xor_5_out), .Cin(n1_bit_adder_5_cout), .Sum(result[12]), .Cout(n1_bit_adder_4_cout));
  xor xor_6 (xor_6_out, sub, B[11]);
  _1_bit_adder u_1_bit_adder_5 (
    .A(A[11]), .B(xor_6_out), .Cin(n1_bit_adder_6_cout), .Sum(result[11]), .Cout(n1_bit_adder_5_cout));
  xor xor_7 (xor_7_out, sub, B[10]);
  _1_bit_adder u_1_bit_adder_6 (
    .A(A[10]), .B(xor_7_out), .Cin(n1_bit_adder_7_cout), .Sum(result[10]), .Cout(n1_bit_adder_6_cout));
  xor xor_8 (xor_8_out, sub, B[9]);
  _1_bit_adder u_1_bit_adder_7 (
    .A(A[9]), .B(xor_8_out), .Cin(n1_bit_adder_8_cout), .Sum(result[9]), .Cout(n1_bit_adder_7_cout));
  xor xor_9 (xor_9_out, sub, B[8]);
  xor xor_10 (xor_10_out, sub, B[7]);
  _1_bit_adder u_1_bit_adder_8 (
    .A(A[8]), .B(xor_9_out), .Cin(n1_bit_adder_9_cout), .Sum(result[8]), .Cout(n1_bit_adder_8_cout));
  _1_bit_adder u_1_bit_adder_9 (
    .A(A[7]), .B(xor_10_out), .Cin(n1_bit_adder_10_cout), .Sum(result[7]), .Cout(n1_bit_adder_9_cout));
  xor xor_11 (xor_11_out, sub, B[6]);
  _1_bit_adder u_1_bit_adder_10 (
    .A(A[6]), .B(xor_11_out), .Cin(n1_bit_adder_11_cout), .Sum(result[6]), .Cout(n1_bit_adder_10_cout));
  xor xor_12 (xor_12_out, sub, B[5]);
  _1_bit_adder u_1_bit_adder_11 (
    .A(A[5]), .B(xor_12_out), .Cin(n1_bit_adder_12_cout), .Sum(result[5]), .Cout(n1_bit_adder_11_cout));
  xor xor_13 (xor_13_out, sub, B[4]);
  _1_bit_adder u_1_bit_adder_12 (
    .A(A[4]), .B(xor_13_out), .Cin(n1_bit_adder_13_cout), .Sum(result[4]), .Cout(n1_bit_adder_12_cout));
  xor xor_14 (xor_14_out, sub, B[3]);
  _1_bit_adder u_1_bit_adder_13 (
    .A(A[3]), .B(xor_14_out), .Cin(n1_bit_adder_14_cout), .Sum(result[3]), .Cout(n1_bit_adder_13_cout));
  xor xor_15 (xor_15_out, sub, B[2]);
  _1_bit_adder u_1_bit_adder_14 (
    .A(A[2]), .B(xor_15_out), .Cin(n1_bit_adder_15_cout), .Sum(result[2]), .Cout(n1_bit_adder_14_cout));
  xor xor_16 (xor_16_out, sub, B[1]);
  _1_bit_adder u_1_bit_adder_15 (
    .A(A[1]), .B(xor_16_out), .Cin(n1_bit_adder_16_cout), .Sum(result[1]), .Cout(n1_bit_adder_15_cout));
  xor xor_17 (xor_17_out, sub, B[0]);
  _1_bit_adder u_1_bit_adder_16 (.A(A[0]), .B(xor_17_out), .Cin(sub), .Sum(result[0]), .Cout(n1_bit_adder_16_cout));

  // Other names for the same wires on the sheet: A1 = A[0]; A2 = A[1]; A3 = A[2]; A4 = A[3]; A5 = A[4]; A6 = A[5];
  //   A7 = A[6]; A8 = A[7]; A9 = A[8]; A10 = A[9]; A11 = A[10]; A12 = A[11]; A13 = A[12]; A14 = A[13]; A15 = A[14];
  //   A16 = A[15]; B1 = B[0]; B2 = B[1]; B3 = B[2]; B4 = B[3]; B5 = B[4]; B6 = B[5]; B7 = B[6]; B8 = B[7]; B9 = B[8];
  //   B10 = B[9]; B11 = B[10]; B12 = B[11]; B13 = B[12]; B14 = B[13]; B15 = B[14]; B16 = B[15]; R1 = result[0];
  //   R2 = result[1]; R3 = result[2]; R4 = result[3]; R5 = result[4]; R6 = result[5]; R7 = result[6]; R8 = result[7];
  //   R9 = result[8]; R10 = result[9]; R11 = result[10]; R12 = result[11]; R13 = result[12]; R14 = result[13];
  //   R15 = result[14]; R16 = result[15]
endmodule

module Equality_Comparator (
  input  [15:0] B,
  input  [15:0] A,
  output out_3
);

  wire xnor_1_out, xnor_2_out, xnor_3_out, xnor_4_out, xnor_5_out, xnor_6_out, xnor_7_out, xnor_8_out,
       xnor_9_out, xnor_10_out, xnor_11_out, xnor_12_out, xnor_13_out, xnor_14_out, xnor_15_out, xnor_16_out;

  xnor xnor_1 (xnor_1_out, A[0], B[0]);
  xnor xnor_2 (xnor_2_out, A[1], B[1]);
  xnor xnor_3 (xnor_3_out, A[2], B[2]);
  xnor xnor_4 (xnor_4_out, A[3], B[3]);
  xnor xnor_5 (xnor_5_out, A[4], B[4]);
  xnor xnor_6 (xnor_6_out, A[5], B[5]);
  xnor xnor_7 (xnor_7_out, A[6], B[6]);
  xnor xnor_8 (xnor_8_out, A[7], B[7]);
  and and_1 (out_3, xnor_1_out, xnor_2_out, xnor_3_out, xnor_4_out, xnor_5_out, xnor_6_out, xnor_7_out, xnor_8_out, xnor_9_out, xnor_10_out, xnor_11_out, xnor_12_out, xnor_13_out, xnor_14_out, xnor_15_out, xnor_16_out);
  xnor xnor_9 (xnor_9_out, A[8], B[8]);
  xnor xnor_10 (xnor_10_out, A[9], B[9]);
  xnor xnor_11 (xnor_11_out, A[10], B[10]);
  xnor xnor_12 (xnor_12_out, A[11], B[11]);
  xnor xnor_13 (xnor_13_out, A[12], B[12]);
  xnor xnor_14 (xnor_14_out, A[13], B[13]);
  xnor xnor_15 (xnor_15_out, A[14], B[14]);
  xnor xnor_16 (xnor_16_out, A[15], B[15]);

  // Other names for the same wires on the sheet: A1 = A[0]; A2 = A[1]; A3 = A[2]; A4 = A[3]; A5 = A[4]; A6 = A[5];
  //   A7 = A[6]; A8 = A[7]; A9 = A[8]; A10 = A[9]; A11 = A[10]; A12 = A[11]; A13 = A[12]; A14 = A[13]; A15 = A[14];
  //   A16 = A[15]; B1 = B[0]; B2 = B[1]; B3 = B[2]; B4 = B[3]; B5 = B[4]; B6 = B[5]; B7 = B[6]; B8 = B[7]; B9 = B[8];
  //   B10 = B[9]; B11 = B[10]; B12 = B[11]; B13 = B[12]; B14 = B[13]; B15 = B[14]; B16 = B[15]
endmodule

module ALU_Adder___PC_bne (
  input  [15:0] PC,
  input  [15:0] imm,
  output [15:0] Address
);

  _16_Adder u_16_adder_1 (.sub(1'b0), .result(Address), .A(PC), .B(imm));  // open: ovf
endmodule

module ALU_PC_J (
  input  [11:0] Jump,
  input  [15:0] PC,
  output [15:0] Jump_Address
);


  assign Jump_Address = {PC[15:12], Jump};
endmodule

module _16_bit_Shift (
  input  [15:0] Input,
  input  Direction,
  output [15:0] result
);

  wire and_1_out, and_3_out, and_4_out, and_5_out, and_6_out, and_7_out, and_8_out, and_9_out, and_10_out,
       and_11_out, and_12_out, and_13_out, and_14_out, and_15_out, and_16_out, and_17_out, and_18_out,
       and_19_out, and_20_out, and_21_out, and_22_out, and_23_out, and_24_out, and_25_out, and_26_out,
       and_27_out, and_28_out, and_30_out, not_1_out;

  not not_1 (not_1_out, Direction);
  and and_1 (and_1_out, Input[0], not_1_out);
  and and_2 (result[0], Direction, Input[1]);
  or or_1 (result[1], and_1_out, and_4_out);
  and and_3 (and_3_out, Input[1], not_1_out);
  and and_4 (and_4_out, Direction, Input[2]);
  and and_5 (and_5_out, Input[2], not_1_out);
  or or_2 (result[2], and_3_out, and_6_out);
  and and_6 (and_6_out, Direction, Input[3]);
  and and_7 (and_7_out, Input[3], not_1_out);
  or or_3 (result[3], and_5_out, and_8_out);
  and and_8 (and_8_out, Direction, Input[4]);
  and and_9 (and_9_out, Input[4], not_1_out);
  or or_4 (result[4], and_7_out, and_10_out);
  and and_10 (and_10_out, Direction, Input[5]);
  or or_5 (result[5], and_9_out, and_11_out);
  and and_11 (and_11_out, Direction, Input[6]);
  and and_12 (and_12_out, Input[5], not_1_out);
  and and_13 (and_13_out, Input[6], not_1_out);
  or or_6 (result[6], and_12_out, and_15_out);
  and and_14 (and_14_out, Input[7], not_1_out);
  and and_15 (and_15_out, Direction, Input[7]);
  or or_7 (result[7], and_13_out, and_16_out);
  and and_16 (and_16_out, Direction, Input[8]);
  and and_17 (and_17_out, Input[8], not_1_out);
  or or_8 (result[8], and_14_out, and_18_out);
  and and_18 (and_18_out, Direction, Input[9]);
  or or_9 (result[9], and_17_out, and_19_out);
  and and_19 (and_19_out, Direction, Input[10]);
  and and_20 (and_20_out, Input[9], not_1_out);
  and and_21 (and_21_out, Input[10], not_1_out);
  or or_10 (result[10], and_20_out, and_23_out);
  and and_22 (and_22_out, Input[11], not_1_out);
  and and_23 (and_23_out, Direction, Input[11]);
  or or_11 (result[11], and_21_out, and_24_out);
  and and_24 (and_24_out, Direction, Input[12]);
  and and_25 (and_25_out, Input[12], not_1_out);
  or or_12 (result[12], and_22_out, and_26_out);
  and and_26 (and_26_out, Direction, Input[13]);
  or or_13 (result[13], and_25_out, and_28_out);
  and and_27 (and_27_out, Input[13], not_1_out);
  and and_28 (and_28_out, Direction, Input[14]);
  and and_29 (result[15], Input[14], not_1_out);
  or or_14 (result[14], and_27_out, and_30_out);
  and and_30 (and_30_out, Direction, Input[15]);

  // Other names for the same wires on the sheet: A1 = Input[0]; A2 = Input[1]; A3 = Input[2]; A4 = Input[3];
  //   A5 = Input[4]; A6 = Input[5]; A7 = Input[6]; A8 = Input[7]; A9 = Input[8]; A10 = Input[9]; A11 = Input[10];
  //   A12 = Input[11]; A13 = Input[12]; A14 = Input[13]; A15 = Input[14]; A16 = Input[15]; R1 = result[0];
  //   R2 = result[1]; R3 = result[2]; R4 = result[3]; R5 = result[4]; R6 = result[5]; R7 = result[6]; R8 = result[7];
  //   R9 = result[8]; R10 = result[9]; R11 = result[10]; R12 = result[11]; R13 = result[12]; R14 = result[13];
  //   R15 = result[14]; R16 = result[15]

  // Notes on the sheet:
  //   left = 0
  //   right = 1
endmodule

module Right_Shifter (
  input  [15:0] Input,
  input  [2:0] in_2,
  output [15:0] Output
);

  wire [15:0] n16_bit_shift_2_result, n16_bit_shift_3_result, n16_bit_shift_4_result, n16_bit_shift_5_result,
       n16_bit_shift_6_result, n16_bit_shift_7_result, n16_bit_shift_9_result, n16_bit_shift_10_result,
       n16_bit_shift_11_result, n16_bit_shift_12_result, n16_bit_shift_13_result, n16_bit_shift_15_result,
       n16_bit_shift_16_result, n16_bit_shift_17_result, n16_bit_shift_18_result, n16_bit_shift_20_result,
       n16_bit_shift_21_result, n16_bit_shift_22_result, n16_bit_shift_24_result, n16_bit_shift_26_result,
       n16_bit_shift_27_result, out0, out1, out2, out3, out4, out5, out6, out7;

  assign out0 = Input;  // Buffer buffer_1, 16 bits wide
  _16_bit_Shift u_16_bit_shift_1 (.Direction(1'b1), .result(out1), .Input(Input));
  _16_bit_Shift u_16_bit_shift_2 (.Direction(1'b1), .result(n16_bit_shift_2_result), .Input(Input));
  _16_bit_Shift u_16_bit_shift_3 (.Direction(1'b1), .result(n16_bit_shift_3_result), .Input(Input));
  _16_bit_Shift u_16_bit_shift_4 (.Direction(1'b1), .result(n16_bit_shift_4_result), .Input(Input));
  _16_bit_Shift u_16_bit_shift_5 (.Direction(1'b1), .result(n16_bit_shift_5_result), .Input(Input));
  _16_bit_Shift u_16_bit_shift_6 (.Direction(1'b1), .result(n16_bit_shift_6_result), .Input(Input));
  _16_bit_Shift u_16_bit_shift_7 (.Direction(1'b1), .result(n16_bit_shift_7_result), .Input(Input));
  _16_bit_Shift u_16_bit_shift_8 (.Direction(1'b1), .result(out2), .Input(n16_bit_shift_2_result));
  _16_bit_Shift u_16_bit_shift_9 (.Direction(1'b1), .result(n16_bit_shift_9_result), .Input(n16_bit_shift_3_result));
  _16_bit_Shift u_16_bit_shift_10 (.Direction(1'b1), .result(n16_bit_shift_10_result), .Input(n16_bit_shift_4_result));
  _16_bit_Shift u_16_bit_shift_11 (.Direction(1'b1), .result(n16_bit_shift_11_result), .Input(n16_bit_shift_5_result));
  _16_bit_Shift u_16_bit_shift_12 (.Direction(1'b1), .result(n16_bit_shift_12_result), .Input(n16_bit_shift_6_result));
  _16_bit_Shift u_16_bit_shift_13 (.Direction(1'b1), .result(n16_bit_shift_13_result), .Input(n16_bit_shift_7_result));
  _16_bit_Shift u_16_bit_shift_14 (.Direction(1'b1), .result(out3), .Input(n16_bit_shift_9_result));
  _16_bit_Shift u_16_bit_shift_15 (.Direction(1'b1), .result(n16_bit_shift_15_result), .Input(n16_bit_shift_10_result));
  _16_bit_Shift u_16_bit_shift_16 (.Direction(1'b1), .result(n16_bit_shift_16_result), .Input(n16_bit_shift_11_result));
  _16_bit_Shift u_16_bit_shift_17 (.Direction(1'b1), .result(n16_bit_shift_17_result), .Input(n16_bit_shift_12_result));
  _16_bit_Shift u_16_bit_shift_18 (.Direction(1'b1), .result(n16_bit_shift_18_result), .Input(n16_bit_shift_13_result));
  _16_bit_Shift u_16_bit_shift_19 (.Direction(1'b1), .result(out4), .Input(n16_bit_shift_15_result));
  _16_bit_Shift u_16_bit_shift_20 (.Direction(1'b1), .result(n16_bit_shift_20_result), .Input(n16_bit_shift_16_result));
  _16_bit_Shift u_16_bit_shift_21 (.Direction(1'b1), .result(n16_bit_shift_21_result), .Input(n16_bit_shift_17_result));
  _16_bit_Shift u_16_bit_shift_22 (.Direction(1'b1), .result(n16_bit_shift_22_result), .Input(n16_bit_shift_18_result));
  _16_bit_Shift u_16_bit_shift_23 (.Direction(1'b1), .result(out5), .Input(n16_bit_shift_20_result));
  _16_bit_Shift u_16_bit_shift_24 (.Direction(1'b1), .result(n16_bit_shift_24_result), .Input(n16_bit_shift_21_result));
  _16_bit_Shift u_16_bit_shift_25 (.Direction(1'b1), .result(out6), .Input(n16_bit_shift_24_result));
  _16_bit_Shift u_16_bit_shift_26 (.Direction(1'b1), .result(n16_bit_shift_26_result), .Input(n16_bit_shift_22_result));
  _16_bit_Shift u_16_bit_shift_27 (.Direction(1'b1), .result(n16_bit_shift_27_result), .Input(n16_bit_shift_26_result));
  _16_bit_Shift u_16_bit_shift_28 (.Direction(1'b1), .result(out7), .Input(n16_bit_shift_27_result));
  Multiplexer #(.select(3), .width(16)) multiplexer_1 (
    .in0(out0), .in1(out1), .in2(out2), .in3(out3), .in4(out4), .in5(out5), .in6(out6), .in7(out7),
    .out(Output), .sel(in_2));  // open: en
endmodule

module Left_Shifter (
  input  [15:0] Input,
  input  [2:0] in_2,
  output [15:0] Output
);

  wire [15:0] n16_bit_shift_2_result, n16_bit_shift_3_result, n16_bit_shift_4_result, n16_bit_shift_5_result,
       n16_bit_shift_6_result, n16_bit_shift_7_result, n16_bit_shift_9_result, n16_bit_shift_10_result,
       n16_bit_shift_11_result, n16_bit_shift_12_result, n16_bit_shift_13_result, n16_bit_shift_15_result,
       n16_bit_shift_16_result, n16_bit_shift_17_result, n16_bit_shift_18_result, n16_bit_shift_20_result,
       n16_bit_shift_21_result, n16_bit_shift_22_result, n16_bit_shift_25_result, n16_bit_shift_26_result,
       n16_bit_shift_27_result, out0, out1, out2, out3, out4, out5, out6, out7;

  assign out0 = Input;  // Buffer buffer_1, 16 bits wide
  _16_bit_Shift u_16_bit_shift_1 (.Direction(1'b0), .result(out1), .Input(Input));
  _16_bit_Shift u_16_bit_shift_2 (.Direction(1'b0), .result(n16_bit_shift_2_result), .Input(Input));
  _16_bit_Shift u_16_bit_shift_3 (.Direction(1'b0), .result(n16_bit_shift_3_result), .Input(Input));
  _16_bit_Shift u_16_bit_shift_4 (.Direction(1'b0), .result(n16_bit_shift_4_result), .Input(Input));
  _16_bit_Shift u_16_bit_shift_5 (.Direction(1'b0), .result(n16_bit_shift_5_result), .Input(Input));
  _16_bit_Shift u_16_bit_shift_6 (.Direction(1'b0), .result(n16_bit_shift_6_result), .Input(Input));
  _16_bit_Shift u_16_bit_shift_7 (.Direction(1'b0), .result(n16_bit_shift_7_result), .Input(Input));
  _16_bit_Shift u_16_bit_shift_8 (.Direction(1'b0), .result(out2), .Input(n16_bit_shift_2_result));
  _16_bit_Shift u_16_bit_shift_9 (.Direction(1'b0), .result(n16_bit_shift_9_result), .Input(n16_bit_shift_3_result));
  _16_bit_Shift u_16_bit_shift_10 (.Direction(1'b0), .result(n16_bit_shift_10_result), .Input(n16_bit_shift_4_result));
  _16_bit_Shift u_16_bit_shift_11 (.Direction(1'b0), .result(n16_bit_shift_11_result), .Input(n16_bit_shift_5_result));
  _16_bit_Shift u_16_bit_shift_12 (.Direction(1'b0), .result(n16_bit_shift_12_result), .Input(n16_bit_shift_6_result));
  _16_bit_Shift u_16_bit_shift_13 (.Direction(1'b0), .result(n16_bit_shift_13_result), .Input(n16_bit_shift_7_result));
  _16_bit_Shift u_16_bit_shift_14 (.Direction(1'b0), .result(out3), .Input(n16_bit_shift_9_result));
  _16_bit_Shift u_16_bit_shift_15 (.Direction(1'b0), .result(n16_bit_shift_15_result), .Input(n16_bit_shift_10_result));
  _16_bit_Shift u_16_bit_shift_16 (.Direction(1'b0), .result(n16_bit_shift_16_result), .Input(n16_bit_shift_11_result));
  _16_bit_Shift u_16_bit_shift_17 (.Direction(1'b0), .result(n16_bit_shift_17_result), .Input(n16_bit_shift_12_result));
  _16_bit_Shift u_16_bit_shift_18 (.Direction(1'b0), .result(n16_bit_shift_18_result), .Input(n16_bit_shift_13_result));
  _16_bit_Shift u_16_bit_shift_19 (.Direction(1'b0), .result(out4), .Input(n16_bit_shift_15_result));
  _16_bit_Shift u_16_bit_shift_20 (.Direction(1'b0), .result(n16_bit_shift_20_result), .Input(n16_bit_shift_16_result));
  _16_bit_Shift u_16_bit_shift_21 (.Direction(1'b0), .result(n16_bit_shift_21_result), .Input(n16_bit_shift_17_result));
  _16_bit_Shift u_16_bit_shift_22 (.Direction(1'b0), .result(n16_bit_shift_22_result), .Input(n16_bit_shift_18_result));
  _16_bit_Shift u_16_bit_shift_23 (.Direction(1'b0), .result(out5), .Input(n16_bit_shift_20_result));
  _16_bit_Shift u_16_bit_shift_24 (.Direction(1'b0), .result(out6), .Input(n16_bit_shift_25_result));
  _16_bit_Shift u_16_bit_shift_25 (.Direction(1'b0), .result(n16_bit_shift_25_result), .Input(n16_bit_shift_21_result));
  _16_bit_Shift u_16_bit_shift_26 (.Direction(1'b0), .result(n16_bit_shift_26_result), .Input(n16_bit_shift_27_result));
  _16_bit_Shift u_16_bit_shift_27 (.Direction(1'b0), .result(n16_bit_shift_27_result), .Input(n16_bit_shift_22_result));
  _16_bit_Shift u_16_bit_shift_28 (.Direction(1'b0), .result(out7), .Input(n16_bit_shift_26_result));
  Multiplexer #(.select(3), .width(16)) multiplexer_1 (
    .in0(out0), .in1(out1), .in2(out2), .in3(out3), .in4(out4), .in5(out5), .in6(out6), .in7(out7),
    .out(Output), .sel(in_2));  // open: en
endmodule

module Register (
  input  Clock,
  input  WriteEnable,
  input  Reset,
  input  [15:0] Input,
  output [15:0] Output
);

  D_Flip_Flop d_ff_1 (.clk(Clock), .D(Input[0]), .Q(Output[0]), .en(WriteEnable), .reset(Reset));  // open: Qn, preset
  D_Flip_Flop d_ff_2 (.clk(Clock), .D(Input[1]), .Q(Output[1]), .en(WriteEnable), .reset(Reset));  // open: Qn, preset
  D_Flip_Flop d_ff_3 (.clk(Clock), .D(Input[2]), .Q(Output[2]), .en(WriteEnable), .reset(Reset));  // open: Qn, preset
  D_Flip_Flop d_ff_4 (.clk(Clock), .D(Input[3]), .Q(Output[3]), .en(WriteEnable), .reset(Reset));  // open: Qn, preset
  D_Flip_Flop d_ff_5 (.clk(Clock), .D(Input[4]), .Q(Output[4]), .en(WriteEnable), .reset(Reset));  // open: Qn, preset
  D_Flip_Flop d_ff_6 (.clk(Clock), .D(Input[5]), .Q(Output[5]), .en(WriteEnable), .reset(Reset));  // open: Qn, preset
  D_Flip_Flop d_ff_7 (.clk(Clock), .D(Input[6]), .Q(Output[6]), .en(WriteEnable), .reset(Reset));  // open: Qn, preset
  D_Flip_Flop d_ff_8 (.clk(Clock), .D(Input[7]), .Q(Output[7]), .en(WriteEnable), .reset(Reset));  // open: Qn, preset
  D_Flip_Flop d_ff_9 (.clk(Clock), .D(Input[8]), .Q(Output[8]), .en(WriteEnable), .reset(Reset));  // open: Qn, preset
  D_Flip_Flop d_ff_10 (.clk(Clock), .D(Input[9]), .Q(Output[9]), .en(WriteEnable), .reset(Reset));  // open: Qn, preset
  D_Flip_Flop d_ff_11 (
    .clk(Clock), .D(Input[10]), .Q(Output[10]), .en(WriteEnable), .reset(Reset));  // open: Qn, preset
  D_Flip_Flop d_ff_12 (
    .clk(Clock), .D(Input[11]), .Q(Output[11]), .en(WriteEnable), .reset(Reset));  // open: Qn, preset
  D_Flip_Flop d_ff_13 (
    .clk(Clock), .D(Input[12]), .Q(Output[12]), .en(WriteEnable), .reset(Reset));  // open: Qn, preset
  D_Flip_Flop d_ff_14 (
    .clk(Clock), .D(Input[13]), .Q(Output[13]), .en(WriteEnable), .reset(Reset));  // open: Qn, preset
  D_Flip_Flop d_ff_15 (
    .clk(Clock), .D(Input[14]), .Q(Output[14]), .en(WriteEnable), .reset(Reset));  // open: Qn, preset
  D_Flip_Flop d_ff_16 (
    .clk(Clock), .D(Input[15]), .Q(Output[15]), .en(WriteEnable), .reset(Reset));  // open: Qn, preset

  // Other names for the same wires on the sheet: Clk = Clock; In1 = Input[0]; In2 = Input[1]; In3 = Input[2];
  //   In4 = Input[3]; In5 = Input[4]; In6 = Input[5]; In7 = Input[6]; In8 = Input[7]; In9 = Input[8]; In10 = Input[9];
  //   In11 = Input[10]; In12 = Input[11]; In13 = Input[12]; In14 = Input[13]; In15 = Input[14]; In16 = Input[15];
  //   out1 = Output[0]; out2 = Output[1]; out3 = Output[2]; out4 = Output[3]; out5 = Output[4]; out6 = Output[5];
  //   out7 = Output[6]; out8 = Output[7]; out9 = Output[8]; out10 = Output[9]; out11 = Output[10]; out12 = Output[11];
  //   out13 = Output[12]; out14 = Output[13]; out15 = Output[14]; out16 = Output[15]; WE = WriteEnable
endmodule

module RegisterFile (
  input  Reset,
  input  [2:0] ReadReg1,
  input  [2:0] ReadReg2,
  input  [15:0] Input,
  input  RegWriteEnable,
  input  Clock,
  input  [2:0] WriteReg,
  output [15:0] ReadData1,
  output [15:0] ReadData2
);

  wire and_1_out, and_2_out, and_3_out, and_4_out, and_5_out, and_6_out, and_7_out, decoder_2_out0,
       decoder_2_out1, decoder_2_out2, decoder_2_out3, decoder_2_out4, decoder_2_out5, decoder_2_out6,
       decoder_2_out7, decoder_3_out0, decoder_3_out1, decoder_3_out2, decoder_3_out3, decoder_3_out4,
       decoder_3_out5, decoder_3_out6, decoder_3_out7, r0, r1_t, r2_t, r3, r4, r5, r6, r7;
  wire [15:0] out0, out1, out2, out3, out4, out5, out6, out7;

  Decoder #(.select(3)) decoder_1 (
    .out0(r0), .out1(r1_t), .out2(r2_t), .out3(r3), .out4(r4), .out5(r5), .out6(r6), .out7(r7), .sel(WriteReg));  // open: en
  and and_1 (and_1_out, r1_t, RegWriteEnable);
  and and_2 (and_2_out, r2_t, RegWriteEnable);
  and and_3 (and_3_out, r3, RegWriteEnable);
  and and_4 (and_4_out, r4, RegWriteEnable);
  and and_5 (and_5_out, r5, RegWriteEnable);
  and and_6 (and_6_out, r6, RegWriteEnable);
  and and_7 (and_7_out, r7, RegWriteEnable);
  Register register_1 (.Clock(Clock), .WriteEnable(1'b0), .Reset(Reset), .Input(Input), .Output(out0));
  Register register_2 (.Clock(Clock), .WriteEnable(and_1_out), .Reset(Reset), .Input(Input), .Output(out1));
  Register register_3 (.Clock(Clock), .WriteEnable(and_2_out), .Reset(Reset), .Input(Input), .Output(out2));
  Register register_4 (.Clock(Clock), .WriteEnable(and_3_out), .Reset(Reset), .Input(Input), .Output(out3));
  Register register_5 (.Clock(Clock), .WriteEnable(and_4_out), .Reset(Reset), .Input(Input), .Output(out4));
  Register register_6 (.Clock(Clock), .WriteEnable(and_5_out), .Reset(Reset), .Input(Input), .Output(out5));
  Register register_7 (.Clock(Clock), .WriteEnable(and_6_out), .Reset(Reset), .Input(Input), .Output(out6));
  Register register_8 (.Clock(Clock), .WriteEnable(and_7_out), .Reset(Reset), .Input(Input), .Output(out7));
  // Probe on out0
  // Probe on out1
  // Probe on out2
  // Probe on out3
  // Probe on out4
  // Probe on out5
  // Probe on out6
  // Probe on out7
  assign ReadData1 = decoder_2_out0 ? out0 : 16'bz;  // Controlled_Buffer controlled_buffer_1
  assign ReadData2 = decoder_3_out0 ? out0 : 16'bz;  // Controlled_Buffer controlled_buffer_2
  assign ReadData1 = decoder_2_out1 ? out1 : 16'bz;  // Controlled_Buffer controlled_buffer_3
  assign ReadData2 = decoder_3_out1 ? out1 : 16'bz;  // Controlled_Buffer controlled_buffer_4
  assign ReadData1 = decoder_2_out2 ? out2 : 16'bz;  // Controlled_Buffer controlled_buffer_5
  assign ReadData2 = decoder_3_out2 ? out2 : 16'bz;  // Controlled_Buffer controlled_buffer_6
  Decoder #(.select(3)) decoder_2 (
    .out0(decoder_2_out0), .out1(decoder_2_out1), .out2(decoder_2_out2), .out3(decoder_2_out3),
    .out4(decoder_2_out4), .out5(decoder_2_out5), .out6(decoder_2_out6), .out7(decoder_2_out7), .sel(ReadReg1));  // open: en
  assign ReadData1 = decoder_2_out3 ? out3 : 16'bz;  // Controlled_Buffer controlled_buffer_7
  Decoder #(.select(3)) decoder_3 (
    .out0(decoder_3_out0), .out1(decoder_3_out1), .out2(decoder_3_out2), .out3(decoder_3_out3),
    .out4(decoder_3_out4), .out5(decoder_3_out5), .out6(decoder_3_out6), .out7(decoder_3_out7), .sel(ReadReg2));  // open: en
  assign ReadData2 = decoder_3_out3 ? out3 : 16'bz;  // Controlled_Buffer controlled_buffer_8
  assign ReadData1 = decoder_2_out4 ? out4 : 16'bz;  // Controlled_Buffer controlled_buffer_9
  assign ReadData2 = decoder_3_out4 ? out4 : 16'bz;  // Controlled_Buffer controlled_buffer_10
  assign ReadData1 = decoder_2_out5 ? out5 : 16'bz;  // Controlled_Buffer controlled_buffer_11
  assign ReadData2 = decoder_3_out5 ? out5 : 16'bz;  // Controlled_Buffer controlled_buffer_12
  assign ReadData1 = decoder_2_out6 ? out6 : 16'bz;  // Controlled_Buffer controlled_buffer_13
  assign ReadData2 = decoder_3_out6 ? out6 : 16'bz;  // Controlled_Buffer controlled_buffer_14
  assign ReadData1 = decoder_2_out7 ? out7 : 16'bz;  // Controlled_Buffer controlled_buffer_15
  assign ReadData2 = decoder_3_out7 ? out7 : 16'bz;  // Controlled_Buffer controlled_buffer_16

  // Other names for the same wires on the sheet: Clk = Clock; data[15:0] = Input; R1[2:0] = ReadReg1;
  //   R2[2:0] = ReadReg2; WE = RegWriteEnable
endmodule

module PC (
  input  [15:0] Address_in,
  input  Clock,
  input  reset,
  output [15:0] Address_out
);

  Register register_1 (.Clock(Clock), .WriteEnable(1'b1), .Reset(reset), .Input(Address_in), .Output(Address_out));
endmodule

module Control (
  input  [3:0] Instr_Optype,
  output keyboard,
  output jal,
  output jump,
  output blt,
  output bne,
  output lw_sw,
  output sw,
  output ALUimm,
  output WE,
  output Rdst,
  output ALUOp,
  output jr,
  output TTYWE
);

  wire decoder_1_out0, decoder_1_out1, decoder_1_out2, decoder_1_out3, decoder_1_out4, decoder_1_out5,
       decoder_1_out6, decoder_1_out11;

  Decoder #(.select(4), .enable("false")) decoder_1 (
    .out0(decoder_1_out0), .out1(decoder_1_out1), .out2(decoder_1_out2), .out3(decoder_1_out3),
    .out4(decoder_1_out4), .out5(decoder_1_out5), .out6(decoder_1_out6), .out7(lw_sw), .out8(sw), .out9(bne),
    .out10(blt), .out11(decoder_1_out11), .out12(jr), .out13(jal), .out14(keyboard), .out15(TTYWE),
    .sel(Instr_Optype));
  or or_1 (jump, jal, decoder_1_out11);
  or or_2 (ALUimm, decoder_1_out1, lw_sw, sw);
  or or_3 (WE, keyboard, lw_sw, decoder_1_out6, decoder_1_out0, decoder_1_out1, decoder_1_out2, decoder_1_out3, decoder_1_out4, decoder_1_out5, jal);
  or or_4 (Rdst, jal, blt, sw, decoder_1_out0, decoder_1_out2, decoder_1_out3, decoder_1_out4, decoder_1_out5, decoder_1_out6, bne);
  or or_5 (ALUOp, sw, lw_sw, decoder_1_out6, decoder_1_out5, decoder_1_out4, decoder_1_out3, decoder_1_out2, decoder_1_out1, decoder_1_out0);
endmodule

module ALU_Control (
  input  Control,
  input  [3:0] ALU_Instruction,
  output [2:0] ALU_optype
);

  wire add_out, addi_out, and_1_out, and_2_out, and_3_out, and_4_out, and_5_out, and_6_out, and_7_out,
       lw_out, not_1_out, not_2_out, not_3_out, not_4_out, not_5_out, not_6_out, not_7_out, not_8_out,
       not_9_out, not_10_out, not_11_out, not_12_out, not_13_out, not_14_out, not_15_out, not_16_out,
       not_17_out, not_18_out, not_19_out, not_20_out, not_21_out, not_22_out, not_23_out, not_24_out,
       or_1_out, or_2_out, sll_out, srl_out, sub_out, sw_out, xor_out;

  not not_1 (not_1_out, ALU_Instruction[0]);
  not not_2 (not_2_out, ALU_Instruction[1]);
  not not_3 (not_3_out, ALU_Instruction[2]);
  not not_4 (not_4_out, ALU_Instruction[3]);
  not not_5 (not_5_out, ALU_Instruction[1]);
  not not_6 (not_6_out, ALU_Instruction[2]);
  not not_7 (not_7_out, ALU_Instruction[3]);
  not not_8 (not_8_out, ALU_Instruction[0]);
  not not_9 (not_9_out, ALU_Instruction[2]);
  not not_10 (not_10_out, ALU_Instruction[3]);
  not not_11 (not_11_out, ALU_Instruction[2]);
  not not_12 (not_12_out, ALU_Instruction[3]);
  not not_13 (not_13_out, ALU_Instruction[0]);
  not not_14 (not_14_out, ALU_Instruction[1]);
  not not_15 (not_15_out, ALU_Instruction[3]);
  not not_16 (not_16_out, ALU_Instruction[1]);
  not not_17 (not_17_out, ALU_Instruction[3]);
  not not_18 (not_18_out, ALU_Instruction[0]);
  not not_19 (not_19_out, ALU_Instruction[3]);
  not not_20 (not_20_out, ALU_Instruction[3]);
  not not_21 (not_21_out, ALU_Instruction[0]);
  not not_22 (not_22_out, ALU_Instruction[1]);
  not not_23 (not_23_out, ALU_Instruction[2]);
  and add (add_out, not_1_out, not_2_out, not_3_out, not_4_out);
  and addi (addi_out, ALU_Instruction[0], not_5_out, not_6_out, not_7_out);
  and sub (sub_out, not_8_out, ALU_Instruction[1], not_9_out, not_10_out);
  and not_24 (not_24_out, ALU_Instruction[0], ALU_Instruction[1], not_11_out, not_12_out);
  and \xor  (xor_out, not_13_out, not_14_out, ALU_Instruction[2], not_15_out);
  and sll (sll_out, ALU_Instruction[0], not_16_out, ALU_Instruction[2], not_17_out);
  and srl (srl_out, not_18_out, ALU_Instruction[1], ALU_Instruction[2], not_19_out);
  and lw (lw_out, ALU_Instruction[0], ALU_Instruction[1], ALU_Instruction[2], not_20_out);
  and sw (sw_out, not_21_out, not_22_out, not_23_out, ALU_Instruction[3]);
  or or_1 (or_1_out, add_out, addi_out);
  and and_1 (and_1_out, sub_out, Control);
  and and_2 (and_2_out, not_24_out, Control);
  and and_3 (and_3_out, xor_out, Control);
  and and_4 (and_4_out, sll_out, Control);
  and and_5 (and_5_out, srl_out, Control);
  or or_2 (or_2_out, lw_out, sw_out);
  and and_6 (and_6_out, or_1_out, Control);
  assign ALU_optype = and_1_out ? 3'b001 : 3'bz;  // Controlled_Buffer controlled_buffer_1
  assign ALU_optype = and_2_out ? 3'b010 : 3'bz;  // Controlled_Buffer controlled_buffer_2
  assign ALU_optype = and_3_out ? 3'b011 : 3'bz;  // Controlled_Buffer controlled_buffer_3
  assign ALU_optype = and_4_out ? 3'b100 : 3'bz;  // Controlled_Buffer controlled_buffer_4
  assign ALU_optype = and_5_out ? 3'b101 : 3'bz;  // Controlled_Buffer controlled_buffer_5
  and and_7 (and_7_out, or_2_out, Control);
  assign ALU_optype = and_7_out ? 3'b000 : 3'bz;  // Controlled_Buffer controlled_buffer_6
  assign ALU_optype = and_6_out ? 3'b000 : 3'bz;  // Controlled_Buffer controlled_buffer_7

  // Other names for the same wires on the sheet: in1 = ALU_Instruction[0]; in2 = ALU_Instruction[1];
  //   in3 = ALU_Instruction[2]; in4 = ALU_Instruction[3]; ctl = Control
endmodule

module MIPS_Instr_Div (
  input  [15:0] MIPS,
  output [2:0] Shamt,
  output [2:0] Rd,
  output [2:0] Rt,
  output [2:0] Rs,
  output [3:0] Opcode,
  output [5:0] Immediate,
  output [11:0] Address
);


  assign Address = MIPS[11:0];
  assign Immediate = MIPS[5:0];
  assign Opcode = MIPS[15:12];
  assign Rd = MIPS[5:3];
  assign Rs = MIPS[11:9];
  assign Rt = MIPS[8:6];
  assign Shamt = MIPS[2:0];
endmodule
